# Fritzing sketch Pinewood layout (saved by Fritzing 0.9.4)
breadboards: 1

parts:
  IC1 = L293D [package=THT]
  S1 = Toggle Switch [package=THT]
  M1 = DC Motor
  R1 = Resistor [tolerance=±5% resistance=220 package="1206 [SMD]"]
  Part1 = Arduino Nano (Rev3.0)
  VCC1 = 4 x AAA Battery Mount
  U1 = LIPO-110mAh [package=lipo-110]  # not connected
  NEOPIXEL1 = Neopixel Strip -- Black (60/m) [part_number=1461]
  Part4 = Adafruit Switched JST Breakout [part_number="Adafruit #1863"]
  Part7 = PowerBoost 1000 Basic
  S2 = Toggle Switch [package=THT]

nets:
  N1: IC1.Enable_1, Part1.D5
  N2: IC1.In_1, Part1.D9
  N3: IC1.Out_1_(_Controlled_by_Enable_1_), M1.pin_2
  GND: IC1.0V, S1.L1, Part1.GND, VCC1.-, NEOPIXEL1.GND, Part4.GND, Part7.GND, S2.L2
  N4: IC1.Out_2_(_Controlled_by_Enable_1_), M1.pin_1
  N5: IC1.In_2, Part1.D4
  N6: IC1.+Vmotor, VCC1.+
  5V: IC1.+V, Part1.5V, NEOPIXEL1.+5V
  N7: S1.L2, Part1.D2
  N8: R1.Pin_0, Part1.D7
  N9: R1.Pin_1, NEOPIXEL1.DI
  N10: Part1.D3, S2.L1
  N11: Part1.VIN, Part7.5.0V
  N12: Part4.SW, Part7.VBAT

custom parts:
  Neopixel Strip -- Black (60/m): Neopixel Strip, Black, 60 pixels per meter.
  Adafruit Switched JST Breakout: This switched JST connector is the best way to quickly prototype with our LiPoly batteries. We paired a genuine JST connector with a slide switch that can do up to 600mA. Both are soldered onto a breadboard-friendly breakout. There's two ground pins, one 'switched' power pin, and one pin that is always on. This is compatible with the "JST PH 2-pin" connectors we use in our battery packs..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
  PowerBoost 1000 Basic: The PowerBoost 1000 is a little DC/DC boost converter module that can run from 1.8V batteries or higher, and convert the battery output to 5.2V DC for running your 5V projects. At its heart is a TPS61030 boost converter from TI. This boost converter chip has some really nice extras such as low battery detection, 4A internal switch, synchronous conversion, excellent efficiency, and 700KHz high-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
